# Fritzing sketch quattrofonti (saved by Fritzing 0.9.2b)
breadboards: 1

parts:
  Part1 = Ns1 Nanosynth by SoundMachines
  S1 = Pushbutton [package="[THT]"]
  S2 = Pushbutton [package="[THT]"]
  LED2 = RGB LED (com. cathode, rgb) [package="5 mm [THT]"]
  R1 = Resistor [tolerance=±5% resistance=680 package="0805 [SMD]"]
  R2 = Resistor [tolerance=±5% resistance=680 package="0805 [SMD]"]
  R3 = Resistor [tolerance=±5% resistance=680 package="0805 [SMD]"]
  R4 = Resistor [tolerance=±5% resistance=680 package="0805 [SMD]"]
  LED3 = smd LED [color="Yellow (592nm)" package="0603 [SMD]"]

nets:
  N1: Part1.GND, R3.Pin_1
  N2: Part1.5V#15, Part1.A, Part1.DDD
  N3: Part1.5V#29, R1.Pin_1
  N4: Part1.0V#30, R2.Pin_1
  N5: Part1.6, R4.Pin_1
  N6: Part1.7, Part1.BT_1
  N7: Part1.9(M), Part1.BT_2
  N8: Part1.10(M), Part1.BT_3
  N9: Part1.11, S1.Pin_3, S1.Pin_4
  N10: Part1.12, S2.Pin_3, S2.Pin_4
  N11: Part1.AAA, Part1.0V#47, Part1.B
  N12: Part1.BBB, Part1.5V#51, Part1.C
  N13: Part1.CCC, Part1.0V#55, Part1.D
  N14: Part1.0V#184, S1.Pin_1, S1.Pin_2, S2.Pin_1, S2.Pin_2, LED2.common_cathode, LED3.cathode
  N15: LED2.red_anode, R3.Pin_0
  N16: LED2.green_anode, R2.Pin_0
  N17: LED2.blue_anode, R1.Pin_0
  N18: R4.Pin_0, LED3.anode

custom parts:
  Ns1 Nanosynth by SoundMachines: The NS1nanosynth synthesizer is tiny 220x85mm analog modular synthesizer coupled with an Arduino Micro platform. NS1nanosynth is a good compromise between complexity and usability. It's a Maker synth, totally hackable and customazable yet a good entry level device, and on a budget.
